// Logisim project minicomputer.circ as structural Verilog: 11 circuits, main circuit main
module main (
  input  [7:0] in_1
);

  Clock clock_1 ();  // open: out
  datapath datapath_1 ();  // open: clk, reset
  ALU alu_1 ();  // open: D1, D2, control, R, carry_out, borrow_out, mult_carry_out, remain, major, equal, minor

  // Notes on the sheet:
  //   big_endian
endmodule

module datapath (
  input  clk,
  input  reset
);

  wire [2:0] alucode, rd, rs, rt;
  wire [3:0] opcode;
  wire [15:0] alu_1_r, c_inst, n_inst, PC_q, registers_database_1_r1, registers_database_1_r2;

  Register #(.width(16)) PC (.D(n_inst), .clk(clk), .Q(PC_q), .clr(reset));  // open: en
  Register #(.width(16)) IR (.D(c_inst), .clk(clk), .Q({alucode, rt, rs, rd, opcode}), .clr(reset));  // open: en
  Register #(.width(16)) MAR (.clk(clk), .clr(reset));  // open: D, en, Q
  Register #(.width(16)) MDR (.clk(clk), .clr(reset));  // open: D, en, Q
  RAM #(.addrWidth(16), .dataWidth(16)) instruction_memory (
    .addr(PC_q), .clk(clk), .dout(c_inst));  // open: we, oe, din
  registers_database registers_database_1 (
    .read_reg1(rs), .read_reg2(rt), .write_reg(rd), .clk(clk), .R1(registers_database_1_r1),
    .R2(registers_database_1_r2));  // open: DATA, reg_write
  ALU alu_1 (
    .D1(registers_database_1_r1), .D2(registers_database_1_r2), .control(alucode), .R(alu_1_r));  // open: carry_out, borrow_out, mult_carry_out, remain, major, equal, minor
  RAM #(.addrWidth(16), .dataWidth(16)) data_memory (
    .addr(alu_1_r), .clk(clk), .din(registers_database_1_r2));  // open: we, oe, dout
endmodule

module registers_database (
  input  [15:0] DATA,
  input  reg_write,
  input  [2:0] read_reg1,
  input  [2:0] read_reg2,
  input  [2:0] write_reg,
  input  clk,
  output [15:0] R1,
  output [15:0] R2
);

  wire decoder_1_out0, decoder_1_out3, decoder_1_out4, decoder_1_out5, decoder_1_out6, decoder_1_out7;
  wire [15:0] register_1_q, register_2_q, register_3_q, register_4_q, register_5_q, register_6_q,
       register_7_q, st_bit_register_1_rec;

  Decoder #(.select(3)) decoder_1 (
    .out0(decoder_1_out0), .out1(decoder_1_out0), .out2(decoder_1_out0), .out3(decoder_1_out3),
    .out4(decoder_1_out4), .out5(decoder_1_out5), .out6(decoder_1_out6), .out7(decoder_1_out7),
    .sel(write_reg), .en(reg_write));
  Register #(.width(16)) register_1 (.D(DATA), .en(decoder_1_out0), .clk(clk), .Q(register_1_q));  // open: clr
  Register #(.width(16)) register_2 (.D(DATA), .en(decoder_1_out4), .clk(clk), .Q(register_2_q));  // open: clr
  Register #(.width(16)) register_3 (.D(DATA), .en(decoder_1_out0), .clk(clk), .Q(register_3_q));  // open: clr
  Register #(.width(16)) register_4 (.D(DATA), .en(decoder_1_out5), .clk(clk), .Q(register_4_q));  // open: clr
  Register #(.width(16)) register_5 (.D(DATA), .en(decoder_1_out0), .clk(clk), .Q(register_5_q));  // open: clr
  Register #(.width(16)) register_6 (.D(DATA), .en(decoder_1_out6), .clk(clk), .Q(register_6_q));  // open: clr
  Register #(.width(16)) register_7 (.D(DATA), .en(decoder_1_out7), .clk(clk), .Q(register_7_q));  // open: clr
  st_bit_register st_bit_register_1 (
    .DATA(DATA), .store(decoder_1_out3), .clk(clk), .REC(st_bit_register_1_rec));  // open: clear
  Multiplexer #(.select(3), .width(16)) multiplexer_1 (
    .in0(register_1_q), .in1(register_3_q), .in2(register_5_q), .in3(st_bit_register_1_rec),
    .in4(register_2_q), .in5(register_4_q), .in6(register_6_q), .in7(register_7_q), .out(R1), .sel(read_reg1));
  Multiplexer #(.select(3), .width(16)) multiplexer_2 (
    .in0(register_1_q), .in1(register_3_q), .in2(register_5_q), .in3(st_bit_register_1_rec),
    .in4(register_2_q), .in5(register_4_q), .in6(register_6_q), .in7(register_7_q), .out(R2), .sel(read_reg2));
endmodule

module st_bit_register (
  input  [15:0] DATA,
  input  clear,
  input  store,
  input  clk,
  output [15:0] REC
);

  wire [15:0] multiplexer_1_out;

  Multiplexer #(.width(16)) multiplexer_1 (.in0(DATA), .in1(REC), .out(multiplexer_1_out), .sel(store));
  eight_bit_register eight_bit_register_1 (.in_1(multiplexer_1_out[15:8]), .clear(clear), .clk(clk), .R(REC[15:8]));
  eight_bit_register eight_bit_register_2 (.in_1(multiplexer_1_out[7:0]), .clear(clear), .clk(clk), .R(REC[7:0]));
endmodule

module eight_bit_register (
  input  [7:0] in_1,
  input  clear,
  input  clk,
  output [7:0] R
);

  flipflop_d flipflop_d_1 (.D(in_1[0]), .clear(clear), .clk(clk), .Q(R[0]));
  flipflop_d flipflop_d_2 (.D(in_1[7]), .clear(clear), .clk(clk), .Q(R[7]));
  flipflop_d flipflop_d_3 (.D(in_1[1]), .clear(clear), .clk(clk), .Q(R[1]));
  flipflop_d flipflop_d_4 (.D(in_1[6]), .clear(clear), .clk(clk), .Q(R[6]));
  flipflop_d flipflop_d_5 (.D(in_1[2]), .clear(clear), .clk(clk), .Q(R[2]));
  flipflop_d flipflop_d_6 (.D(in_1[5]), .clear(clear), .clk(clk), .Q(R[5]));
  flipflop_d flipflop_d_7 (.D(in_1[3]), .clear(clear), .clk(clk), .Q(R[3]));
  flipflop_d flipflop_d_8 (.D(in_1[4]), .clear(clear), .clk(clk), .Q(R[4]));
endmodule

module flipflop_d (
  input  D,
  input  clear,
  input  clk,
  output Q
);

  wire master_latch_q, not_1_out;

  not not_1 (not_1_out, clk);
  latch_d master_latch (.D(D), .reset(clear), .E(not_1_out), .Q(master_latch_q));  // open: NQ
  latch_d slave_latch (.D(master_latch_q), .reset(clear), .E(clk), .Q(Q));  // open: NQ
endmodule

module latch_d (
  input  D,
  input  reset,
  input  E,
  output Q,
  output NQ
);

  wire nand_1_out, nand_2_out, not_1_out, not_2_out;

  not not_1 (not_1_out, D);
  nand nand_1 (nand_1_out, D, E);
  nand nand_2 (nand_2_out, E, not_1_out);
  not not_2 (not_2_out, reset);
  nand nand_3 (Q, nand_1_out, NQ);
  nand nand_4 (NQ, Q, not_2_out, nand_2_out);
endmodule

module ALU (
  input  [15:0] D1,
  input  [15:0] D2,
  input  [2:0] control,
  output [15:0] R,
  output carry_out,
  output borrow_out,
  output [15:0] mult_carry_out,
  output [15:0] remain,
  output major,
  output equal,
  output minor
);

  wire LSA_carry_out;
  wire [7:0] LSA_out_4, MSA_out_4;
  wire [15:0] and_1_out, divider_1_out, multiplier_1_out, or_1_out, shifter_1_out, shifter_2_out,
       subtractor_1_out;

  Comparator #(.width(16)) comparator_1 (.a(D1), .b(D2), .gt(major), .eq(equal), .lt(minor));
  eight_bit_adder LSA (.in_1(1'b0), .D1(D1[7:0]), .D2(D2[7:0]), .out_4(LSA_out_4), .carry_out(LSA_carry_out));
  eight_bit_adder MSA (.in_1(LSA_carry_out), .D1(D1[15:8]), .D2(D2[15:8]), .out_4(MSA_out_4), .carry_out(carry_out));
  Subtractor #(.width(16)) subtractor_1 (.a(D1), .b(D2), .out(subtractor_1_out), .bin(1'b0), .bout(borrow_out));
  Multiplier #(.width(16)) multiplier_1 (
    .a(D1), .b(D2), .out(multiplier_1_out), .cin({16{1'b0}}), .cout(mult_carry_out));
  Divider #(.width(16)) divider_1 (.a(D1), .b(D2), .out(divider_1_out), .upper({16{1'b0}}), .rem(remain));
  Shifter #(.shift("lr"), .width(16)) shifter_1 (.out(shifter_1_out));  // open: in, dist
  Shifter #(.width(16)) shifter_2 (.in(D1), .\dist (D2[3:0]), .out(shifter_2_out));
  assign and_1_out = D2 & D1;  // AND_Gate and_1, 16 bits wide
  assign or_1_out = D2 | D1;  // OR_Gate or_1, 16 bits wide
  Multiplexer #(.select(3), .width(16)) multiplexer_1 (
    .in0({MSA_out_4, LSA_out_4}), .in1(subtractor_1_out), .in2(multiplier_1_out), .in3(divider_1_out),
    .in4(and_1_out), .in5(or_1_out), .in6(shifter_1_out), .in7(shifter_2_out), .out(R), .sel(control));

  // Notes on the sheet:
  //   sub
  //   mult
  //   div
  //   add
  //   or
  //   and
  //   shft_r
  //   shift_l
endmodule

module eight_bit_adder (
  input  in_1,
  input  [7:0] D1,
  input  [7:0] D2,
  output [7:0] out_4,
  output carry_out
);

  wire full_adder_1_co, full_adder_2_co, full_adder_3_co, full_adder_4_co, full_adder_5_co, full_adder_6_co,
       full_adder_7_co;

  full_adder full_adder_1 (.A(D1[0]), .B(D2[0]), .CI(in_1), .CO(full_adder_1_co), .S(out_4[0]));
  full_adder full_adder_2 (.A(D1[4]), .B(D2[4]), .CI(full_adder_7_co), .CO(full_adder_2_co), .S(out_4[4]));
  full_adder full_adder_3 (.A(D1[1]), .B(D2[1]), .CI(full_adder_1_co), .CO(full_adder_3_co), .S(out_4[1]));
  full_adder full_adder_4 (.A(D1[5]), .B(D2[5]), .CI(full_adder_2_co), .CO(full_adder_4_co), .S(out_4[5]));
  full_adder full_adder_5 (.A(D1[2]), .B(D2[2]), .CI(full_adder_3_co), .CO(full_adder_5_co), .S(out_4[2]));
  full_adder full_adder_6 (.A(D1[6]), .B(D2[6]), .CI(full_adder_4_co), .CO(full_adder_6_co), .S(out_4[6]));
  full_adder full_adder_7 (.A(D1[3]), .B(D2[3]), .CI(full_adder_5_co), .CO(full_adder_7_co), .S(out_4[3]));
  full_adder full_adder_8 (.A(D1[7]), .B(D2[7]), .CI(full_adder_6_co), .CO(carry_out), .S(out_4[7]));

  // Notes on the sheet:
  //   result
endmodule

module full_adder (
  input  A,
  input  B,
  input  CI,
  output CO,
  output S
);

  wire half_adder_1_c, half_adder_1_s, half_adder_2_c;

  half_adder half_adder_1 (.A(A), .B(B), .C(half_adder_1_c), .S(half_adder_1_s));
  half_adder half_adder_2 (.A(half_adder_1_s), .B(CI), .C(half_adder_2_c), .S(S));
  or or_1 (CO, half_adder_1_c, half_adder_2_c);
endmodule

module half_adder (
  input  A,
  input  B,
  output C,
  output S
);

  and and_1 (C, A, B);
  xor xor_1 (S, A, B);
endmodule
