// Logisim project architecture.circ as structural Verilog: 7 circuits, main circuit main
module main (
  input  in_1
);

  wire clock_1_out, datapath_1_readmemory, datapath_1_writememory;
  wire [15:0] bus_control_output_data, datapath_1_memory_address, datapath_1_memory_output;

  Clock clock_1 (.out(clock_1_out));
  datapath datapath_1 (
    .memory_input(bus_control_output_data), .reset(in_1), .clk(clock_1_out),
    .memory_address(datapath_1_memory_address), .memory_output(datapath_1_memory_output),
    .writeMemory(datapath_1_writememory), .readMemory(datapath_1_readmemory));
  memory bus_control (
    .memory_address(datapath_1_memory_address), .input_data(datapath_1_memory_output),
    .write(datapath_1_writememory), .load(datapath_1_readmemory), .clk(clock_1_out),
    .output_data(bus_control_output_data));
endmodule

module datapath (
  input  [15:0] memory_input,
  input  reset,
  input  clk,
  output [15:0] memory_address,
  output [15:0] memory_output,
  output writeMemory,
  output readMemory
);

  wire outALU, outImmediate, outMDR, outPC, priority_encoder_1_en_out, weReg;
  wire [1:0] priority_encoder_1_out, sourcePC;
  wire [2:0] ALUop, writeRegAddr;
  wire [3:0] ALUflags;
  wire [4:0] control_unit_1_we_control;
  wire [5:0] readRegsAddr;
  wire [15:0] adder_1_out, ALUResult, currentInstruction, currentInstructionAddr, immediateValue, IR_q,
       multiplexer_3_out, nextInstructionAddr, registers_database_1_r1, registers_database_1_r2,
       stackInstructionAddr;

  control_unit control_unit_1 (
    .instruction(IR_q), .ALU_flags(ALUflags), .freeze(1'b0), .reset(reset), .clk(clk),
    .immediate(immediateValue), .reg_write(writeRegAddr), .reg_read_A(readRegsAddr[2:0]),
    .reg_read_B(readRegsAddr[5:3]), .mem_control({writeMemory, readMemory}), .pcSource(sourcePC),
    .ALU_op(ALUop), .we_control({weReg, control_unit_1_we_control}),
    .out_control({outImmediate, outALU, outMDR, outPC}));
  Register #(.width(16)) IR (
    .D(currentInstruction), .en(control_unit_1_we_control[0]), .clk(clk), .Q(IR_q), .clr(reset));
  Register #(.width(16)) PC (
    .D(nextInstructionAddr), .en(control_unit_1_we_control[1]), .clk(clk), .Q(currentInstructionAddr),
    .clr(reset));
  Register #(.width(16)) SP (
    .D(memory_output), .en(control_unit_1_we_control[2]), .clk(clk), .Q(stackInstructionAddr), .clr(reset));
  Register #(.width(16)) MAR (
    .D(currentInstructionAddr), .en(control_unit_1_we_control[3]), .clk(clk), .Q(memory_address), .clr(reset));
  Register #(.width(16)) MDR (
    .D(memory_input), .en(control_unit_1_we_control[4]), .clk(clk), .Q(currentInstruction), .clr(reset));
  Adder #(.width(16)) adder_1 (.a(16'h1), .b(currentInstructionAddr), .out(adder_1_out));  // open: cin, cout
  Priority_Encoder #(.select(2)) priority_encoder_1 (
    .in0(outPC), .in1(outMDR), .in2(outALU), .in3(outImmediate), .out(priority_encoder_1_out),
    .en_out(priority_encoder_1_en_out), .en_in(1'b1));  // open: gs
  Multiplexer #(.select(2), .width(16)) multiplexer_1 (
    .in0(adder_1_out), .in1(immediateValue), .in2(stackInstructionAddr), .in3(ALUResult),
    .out(nextInstructionAddr), .sel(sourcePC));
  registers_database registers_database_1 (
    .DATA(memory_output), .write(weReg), .read_reg1_addr(readRegsAddr[2:0]),
    .read_reg2_addr(readRegsAddr[5:3]), .write_reg_addr(writeRegAddr), .clk(clk),
    .R1(registers_database_1_r1), .R2(registers_database_1_r2));
  Multiplexer #(.select(2), .width(16)) multiplexer_2 (
    .in0(nextInstructionAddr), .in1(currentInstruction), .in2(ALUResult), .in3(immediateValue),
    .out(memory_output), .sel(priority_encoder_1_out));
  Multiplexer #(.width(16)) multiplexer_3 (
    .in0(registers_database_1_r2), .in1(immediateValue), .out(multiplexer_3_out), .sel(outImmediate));
  ALU alu_1 (
    .D1(registers_database_1_r1), .D2(multiplexer_3_out), .op_control(ALUop), .ALUflags(ALUflags),
    .Res1(ALUResult));  // open: carry_in, Res2
  // also tied to VCC on the sheet: priority_encoder_1_en_out

  // Other names for the same wires on the sheet: readMem = readMemory; writeMem = writeMemory; clock = clk;
  //   memoryAddressOut[15:0] = memory_address; memoryDataIn[15:0] = memory_input; dataBus[15:0] = memory_output;
  //   memoryDataOut[15:0] = memory_output
endmodule

module ALU (
  input  [15:0] D1,
  input  [15:0] D2,
  input  [15:0] carry_in,
  input  [2:0] op_control,
  output [15:0] Res1,
  output [15:0] Res2,
  output [3:0] ALUflags
);

  wire addOverflow, borrowOut, carryOut, not_1_out, not_2_out, subOverflow, xor_1_out, xor_2_out, xor_3_out,
       xor_4_out;
  wire [15:0] adder_1_out, and_3_out, divider_1_out, divRemain, multCarryOut, multiplier_1_out, or_1_out,
       shifter_1_out, shifter_2_out, subtractor_1_out;

  Adder #(.width(16)) adder_1 (.a(D1), .b(D2), .out(adder_1_out), .cin(carry_in[0]), .cout(carryOut));
  Subtractor #(.width(16)) subtractor_1 (.a(D1), .b(D2), .out(subtractor_1_out), .bin(carry_in[0]), .bout(borrowOut));
  Multiplier #(.width(16)) multiplier_1 (.a(D1), .b(D2), .out(multiplier_1_out), .cin(carry_in), .cout(multCarryOut));
  Divider #(.width(16)) divider_1 (.a(D1), .b(D2), .out(divider_1_out), .upper(carry_in), .rem(divRemain));
  Shifter #(.shift("lr"), .width(16)) shifter_1 (.in(D1), .\dist (D2[3:0]), .out(shifter_1_out));
  Shifter #(.width(16)) shifter_2 (.in(D1), .\dist (D2[3:0]), .out(shifter_2_out));
  not not_1 (not_1_out, xor_1_out);
  xor xor_1 (xor_1_out, D1[15], D2[15]);
  xor xor_2 (xor_2_out, D1[15], ALUflags[1]);
  xor xor_3 (xor_3_out, D1[15], D2[15]);
  xor xor_4 (xor_4_out, D1[15], ALUflags[1]);
  and and_1 (addOverflow, not_1_out, xor_2_out);
  and and_2 (subOverflow, xor_3_out, xor_4_out);
  assign and_3_out = D2 & D1;  // AND_Gate and_3, 16 bits wide
  assign or_1_out = D2 | D1;  // OR_Gate or_1, 16 bits wide
  not not_2 (not_2_out, borrowOut);
  Multiplexer #(.select(3), .width(16)) multiplexer_1 (
    .in0(adder_1_out), .in1(subtractor_1_out), .in2(multiplier_1_out), .in3(divider_1_out), .in4(and_3_out),
    .in5(or_1_out), .in6(shifter_1_out), .in7(shifter_2_out), .out({ALUflags[1], Res1[14:0]}),
    .sel(op_control));
  Multiplexer #(.select(3), .width(16)) multiplexer_2 (
    .in0({16{1'b0}}), .in1({16{1'b0}}), .in2(multCarryOut), .in3(divRemain), .in4({16{1'b0}}),
    .in5({16{1'b0}}), .in6({16{1'b0}}), .in7({16{1'b0}}), .out(Res2), .sel(op_control));
  Multiplexer #(.select(3)) multiplexer_3 (
    .in0(carryOut), .in1(not_2_out), .in2(1'b0), .in3(1'b0), .in4(1'b0), .in5(1'b0), .in6(1'b0), .in7(1'b0),
    .out(ALUflags[2]), .sel(op_control));
  Multiplexer #(.select(3)) multiplexer_4 (
    .in0(addOverflow), .in1(subOverflow), .in2(1'b0), .in3(1'b0), .in4(1'b0), .in5(1'b0), .in6(1'b0),
    .in7(1'b0), .out(ALUflags[3]), .sel(op_control));
  nor nor_1 (ALUflags[0], Res1[7], Res1[0], Res1[1], Res1[2], Res1[3], Res1[4], Res1[5], Res1[6], Res1[8], Res1[9], Res1[10], Res1[11], Res1[12], Res1[13], Res1[14], ALUflags[1]);

  assign Res1[15] = ALUflags[1];

  // Other names for the same wires on the sheet: flagZero = ALUflags[0]; flagCarry = ALUflags[2];
  //   flagOverflow = ALUflags[3]; A = D1[15]; B = D2[15]; flagNegative = ALUflags[1]; R = ALUflags[1]

  // Notes on the sheet:
  //   sub
  //   mult
  //   div
  //   add
  //   or
  //   and
  //   shft_r
  //   shift_l
endmodule

module control_unit (
  input  [15:0] instruction,
  input  [3:0] ALU_flags,
  input  freeze,
  input  reset,
  input  clk,
  output [15:0] immediate,
  output [2:0] reg_write,
  output [2:0] reg_read_A,
  output [2:0] reg_read_B,
  output [1:0] mem_control,
  output [1:0] pcSource,
  output [2:0] ALU_op,
  output [5:0] we_control,
  output [3:0] out_control
);

  wire weState;
  wire [2:0] control_decoder_1_next_state, StateRegister_q;

  not not_1 (weState, freeze);
  Multiplexer #(.width(3)) multiplexer_1 (.in0(instruction[9:7]), .in1(3'b000), .out(reg_read_A), .sel(out_control[3]));
  Multiplexer #(.width(3)) multiplexer_2 (.in0(instruction[15:13]), .in1(3'b000), .out(ALU_op), .sel(out_control[2]));
  Multiplexer #(.width(3)) multiplexer_3 (.in0(instruction[6:4]), .in1(3'b000), .out(reg_write), .sel(we_control[5]));
  Multiplexer #(.width(3)) multiplexer_4 (
    .in0(instruction[12:10]), .in1(3'b000), .out(reg_read_B), .sel(out_control[3]));
  Multiplexer #(.width(9)) multiplexer_5 (
    .in0({9{1'b0}}), .in1(instruction[15:7]), .out(immediate[8:0]), .sel(out_control[3]));
  Register #(.width(3)) StateRegister (
    .D(control_decoder_1_next_state), .en(weState), .clk(clk), .Q(StateRegister_q), .clr(reset));
  control_decoder control_decoder_1 (
    .state(StateRegister_q), .opcode(instruction[3:0]), .ALU_flags(ALU_flags),
    .next_state(control_decoder_1_next_state),
    .signals({out_control, mem_control[0], mem_control[1], we_control[5], we_control[0], we_control[4:1], pcSource}));

  assign immediate[15:9] = {7{1'b0}};

  // Other names for the same wires on the sheet: sourcePC[1:0] = pcSource; loadPC = we_control[1];
  //   loadSP = we_control[2]; loadMAR = we_control[3]; loadMDR = we_control[4]; loadIR = we_control[0];
  //   weReg = we_control[5]; memRead = mem_control[1]; memWrite = mem_control[0]; outPC = out_control[0];
  //   outMDR = out_control[1]; outALU = out_control[2]; outImmediate = out_control[3]; ALUoperation[2:0] = ALU_op;
  //   clock = clk; flagsALU[3:0] = ALU_flags; flagZero = ALU_flags[0]; flagNegative = ALU_flags[1];
  //   flagCarry = ALU_flags[2]; flagOverflow = ALU_flags[3]; immediate16b[8:0] = immediate[8:0];
  //   opcode[3:0] = instruction[3:0]; rt[2:0] = instruction[6:4]; immediateValue[8:0] = instruction[15:7];
  //   rs1[2:0] = instruction[9:7]; rs2[2:0] = instruction[12:10]; aluop[2:0] = instruction[15:13];
  //   readRegA[2:0] = reg_read_A; readRegB[2:0] = reg_read_B; writeReg[2:0] = reg_write
endmodule

module control_decoder (
  input  [2:0] state,
  input  [3:0] opcode,
  input  [3:0] ALU_flags,
  output [2:0] next_state,
  output [13:0] signals
);

  ROM #(.addrWidth(11), .dataWidth(3)) stateROM (.addr({ALU_flags, opcode, state}), .data(next_state));
  ROM #(.addrWidth(7), .dataWidth(14)) controlROM (.addr({opcode, state}), .data(signals));

  // Other names for the same wires on the sheet: currentState[2:0] = state;
  //   romAddr[10:0] = {ALU_flags, opcode, state}; nextState[2:0] = next_state; flagsALU[3:0] = ALU_flags;
  //   romSignals[13:0] = signals

  // Notes on the sheet:
  //   contents of stateROM (hex, n*v repeats v):
  //   256*1 256*2 256*3 256*4 16*1 16*5 16*7 80*5 17*1 5 1 5 1 5 1 5 1 5 1 5 1 5 1 5 5 1 5 1 5 1 5 1 5 1 5
  //   1 5 1 5 1 1 1 5 5 1 1 5 5 1 1 5 5 1 1 4*5 1 1 5 5 1 1 5 5 1 1 5 5 4*1 5 5 1 1 5 5 1 1 5 5 1 1 4*5 1
  //   1 5 5 1 1 5 5 1 1 5 5 1 1 16*4 16*0 16*7 16*0 16*7 64*6 16*0 96*1 80*0 16*7 32*1 16*7 128*0 256*1
  //   contents of controlROM (hex, n*v repeats v):
  //   16*0 16*208 16*120 16*884 8*0 2801 8*0 2 0 2 202 202 402 402 0 6*1802 5*0 120 10 212 322 9*0 42 41
  //   42 44 0 0 44
endmodule

module memory (
  input  [15:0] memory_address,
  input  [15:0] input_data,
  input  write,
  input  load,
  input  clk,
  output [15:0] output_data
);

  RAM #(.addrWidth(16), .dataWidth(16)) ram_memory (
    .addr(memory_address), .we(write), .oe(load), .clk(clk), .din(input_data), .dout(output_data));

  // Notes on the sheet:
  //   order: big_endian
endmodule

module registers_database (
  input  [15:0] DATA,
  input  write,
  input  [2:0] read_reg1_addr,
  input  [2:0] read_reg2_addr,
  input  [2:0] write_reg_addr,
  input  clk,
  output [15:0] R1,
  output [15:0] R2
);

  wire decoder_1_out0, decoder_1_out1, decoder_1_out2, decoder_1_out3, decoder_1_out4, decoder_1_out5,
       decoder_1_out6, decoder_1_out7;
  wire [15:0] register_1_q, register_2_q, register_3_q, register_4_q, register_5_q, register_6_q,
       register_7_q, register_8_q;

  Decoder #(.select(3)) decoder_1 (
    .out0(decoder_1_out0), .out1(decoder_1_out1), .out2(decoder_1_out2), .out3(decoder_1_out3),
    .out4(decoder_1_out4), .out5(decoder_1_out5), .out6(decoder_1_out6), .out7(decoder_1_out7),
    .sel(write_reg_addr), .en(write));
  Register #(.width(16)) register_1 (.D({16{1'b0}}), .en(decoder_1_out0), .clk(clk), .Q(register_1_q));  // open: clr
  Register #(.width(16)) register_2 (.D(DATA), .en(decoder_1_out4), .clk(clk), .Q(register_2_q));  // open: clr
  Register #(.width(16)) register_3 (.D(DATA), .en(decoder_1_out1), .clk(clk), .Q(register_3_q));  // open: clr
  Register #(.width(16)) register_4 (.D(DATA), .en(decoder_1_out5), .clk(clk), .Q(register_4_q));  // open: clr
  Register #(.width(16)) register_5 (.D(DATA), .en(decoder_1_out2), .clk(clk), .Q(register_5_q));  // open: clr
  Register #(.width(16)) register_6 (.D(DATA), .en(decoder_1_out6), .clk(clk), .Q(register_6_q));  // open: clr
  Register #(.width(16)) register_7 (.D(DATA), .en(decoder_1_out3), .clk(clk), .Q(register_7_q));  // open: clr
  Register #(.width(16)) register_8 (.D(DATA), .en(decoder_1_out7), .clk(clk), .Q(register_8_q));  // open: clr
  Multiplexer #(.select(3), .width(16)) multiplexer_1 (
    .in0(register_1_q), .in1(register_3_q), .in2(register_5_q), .in3(register_7_q), .in4(register_2_q),
    .in5(register_4_q), .in6(register_6_q), .in7(register_8_q), .out(R1), .sel(read_reg1_addr));
  Multiplexer #(.select(3), .width(16)) multiplexer_2 (
    .in0(register_1_q), .in1(register_3_q), .in2(register_5_q), .in3(register_7_q), .in4(register_2_q),
    .in5(register_4_q), .in6(register_6_q), .in7(register_8_q), .out(R2), .sel(read_reg2_addr));

  // Other names for the same wires on the sheet: rReg1Addr[2:0] = read_reg1_addr; rReg2Addr[2:0] = read_reg2_addr
endmodule
