// Logisim project my_own_circuits.circ as structural Verilog: 10 circuits, main circuit main
module main (
  input  [15:0] in_1,
  input  in_2,
  input  in_3,
  input  in_4,
  input  [15:0] in_5,
  input  [15:0] in_6,
  input  [15:0] in_7,
  input  [2:0] in_8
);

  wire alu_1_borrow_out, alu_1_carry_out, alu_1_equal, alu_1_major, alu_1_minor;
  wire [15:0] alu_1_mult_carry_out, alu_1_r, alu_1_remain, sixteen_bit_register_1_rec;

  ALU alu_1 (
    .carry_in(in_5), .D1(in_6), .D2(in_7), .control(in_8), .R(alu_1_r), .carry_out(alu_1_carry_out),
    .borrow_out(alu_1_borrow_out), .mult_carry_out(alu_1_mult_carry_out), .remain(alu_1_remain),
    .major(alu_1_major), .equal(alu_1_equal), .minor(alu_1_minor));
  // Probe on sixteen_bit_register_1_rec
  sixteen_bit_register sixteen_bit_register_1 (
    .DATA(in_1), .clear(in_2), .write(in_3), .clk(in_4), .REC(sixteen_bit_register_1_rec));
  // Probe on alu_1_carry_out
  // Probe on alu_1_borrow_out
  // Probe on alu_1_mult_carry_out
  // Probe on alu_1_remain
  // Probe on alu_1_major
  // Probe on alu_1_equal
  // Probe on alu_1_minor
  // Probe on alu_1_r
endmodule

module ALU (
  input  [15:0] carry_in,
  input  [15:0] D1,
  input  [15:0] D2,
  input  [2:0] control,
  output [15:0] R,
  output carry_out,
  output borrow_out,
  output [15:0] mult_carry_out,
  output [15:0] remain,
  output major,
  output equal,
  output minor
);

  wire [15:0] and_1_out, divider_1_out, multiplier_1_out, or_1_out, shifter_1_out, shifter_2_out,
       sixteen_bit_adder_1_r, subtractor_1_out;

  Comparator #(.width(16)) comparator_1 (.a(D1), .b(D2), .gt(major), .eq(equal), .lt(minor));
  Subtractor #(.width(16)) subtractor_1 (.a(D1), .b(D2), .out(subtractor_1_out), .bin(carry_in[0]), .bout(borrow_out));
  Multiplier #(.width(16)) multiplier_1 (.a(D1), .b(D2), .out(multiplier_1_out), .cin(carry_in), .cout(mult_carry_out));
  Divider #(.width(16)) divider_1 (.a(D1), .b(D2), .out(divider_1_out), .upper(carry_in), .rem(remain));
  Shifter #(.shift("lr"), .width(16)) shifter_1 (.out(shifter_1_out));  // open: in, dist
  Shifter #(.width(16)) shifter_2 (.in(D1), .\dist (D2[3:0]), .out(shifter_2_out));
  sixteen_bit_adder sixteen_bit_adder_1 (
    .carry_in(carry_in[0]), .D1(D1), .D2(D2), .R(sixteen_bit_adder_1_r), .carry_out(carry_out));
  assign and_1_out = D2 & D1;  // AND_Gate and_1, 16 bits wide
  assign or_1_out = D2 | D1;  // OR_Gate or_1, 16 bits wide
  Multiplexer #(.select(3), .width(16)) multiplexer_1 (
    .in0(sixteen_bit_adder_1_r), .in1(subtractor_1_out), .in2(multiplier_1_out), .in3(divider_1_out),
    .in4(and_1_out), .in5(or_1_out), .in6(shifter_1_out), .in7(shifter_2_out), .out(R), .sel(control));

  // Notes on the sheet:
  //   sub
  //   mult
  //   div
  //   add
  //   or
  //   and
  //   shft_r
  //   shift_l
endmodule

module sixteen_bit_register (
  input  [15:0] DATA,
  input  clear,
  input  write,
  input  clk,
  output [15:0] REC
);

  wire not_1_out;
  wire [15:0] multiplexer_1_out;

  not not_1 (not_1_out, write);
  Multiplexer #(.width(16)) multiplexer_1 (.in0(DATA), .in1(REC), .out(multiplexer_1_out), .sel(not_1_out));
  eight_bit_register MSR (.in_1(multiplexer_1_out[15:8]), .clear(clear), .clk(clk), .R(REC[15:8]));
  eight_bit_register LSR (.in_1(multiplexer_1_out[7:0]), .clear(clear), .clk(clk), .R(REC[7:0]));
endmodule

module eight_bit_register (
  input  [7:0] in_1,
  input  clear,
  input  clk,
  output [7:0] R
);

  flipflop_d flipflop_d_1 (.D(in_1[0]), .clear(clear), .clk(clk), .Q(R[0]));
  flipflop_d flipflop_d_2 (.D(in_1[7]), .clear(clear), .clk(clk), .Q(R[7]));
  flipflop_d flipflop_d_3 (.D(in_1[1]), .clear(clear), .clk(clk), .Q(R[1]));
  flipflop_d flipflop_d_4 (.D(in_1[6]), .clear(clear), .clk(clk), .Q(R[6]));
  flipflop_d flipflop_d_5 (.D(in_1[2]), .clear(clear), .clk(clk), .Q(R[2]));
  flipflop_d flipflop_d_6 (.D(in_1[5]), .clear(clear), .clk(clk), .Q(R[5]));
  flipflop_d flipflop_d_7 (.D(in_1[3]), .clear(clear), .clk(clk), .Q(R[3]));
  flipflop_d flipflop_d_8 (.D(in_1[4]), .clear(clear), .clk(clk), .Q(R[4]));
endmodule

module flipflop_d (
  input  D,
  input  clear,
  input  clk,
  output Q
);

  wire master_latch_q, not_1_out;

  not not_1 (not_1_out, clk);
  latch_d master_latch (.D(D), .reset(clear), .E(not_1_out), .Q(master_latch_q));  // open: NQ
  latch_d slave_latch (.D(master_latch_q), .reset(clear), .E(clk), .Q(Q));  // open: NQ
endmodule

module latch_d (
  input  D,
  input  reset,
  input  E,
  output Q,
  output NQ
);

  wire nand_1_out, nand_2_out, not_1_out, not_2_out;

  not not_1 (not_1_out, D);
  nand nand_1 (nand_1_out, D, E);
  nand nand_2 (nand_2_out, E, not_1_out);
  not not_2 (not_2_out, reset);
  nand nand_3 (Q, nand_1_out, NQ);
  nand nand_4 (NQ, Q, not_2_out, nand_2_out);
endmodule

module sixteen_bit_adder (
  input  carry_in,
  input  [15:0] D1,
  input  [15:0] D2,
  output [15:0] R,
  output carry_out
);

  wire LSA_carry_out;

  eight_bit_adder LSA (.carry_in(carry_in), .D1(D1[7:0]), .D2(D2[7:0]), .R(R[7:0]), .carry_out(LSA_carry_out));
  eight_bit_adder MSA (.carry_in(LSA_carry_out), .D1(D1[15:8]), .D2(D2[15:8]), .R(R[15:8]), .carry_out(carry_out));
endmodule

module eight_bit_adder (
  input  carry_in,
  input  [7:0] D1,
  input  [7:0] D2,
  output [7:0] R,
  output carry_out
);

  wire full_adder_1_co, full_adder_2_co, full_adder_3_co, full_adder_4_co, full_adder_5_co, full_adder_6_co,
       full_adder_7_co;

  full_adder full_adder_1 (.A(D1[0]), .B(D2[0]), .CI(carry_in), .CO(full_adder_1_co), .S(R[0]));
  full_adder full_adder_2 (.A(D1[4]), .B(D2[4]), .CI(full_adder_7_co), .CO(full_adder_2_co), .S(R[4]));
  full_adder full_adder_3 (.A(D1[1]), .B(D2[1]), .CI(full_adder_1_co), .CO(full_adder_3_co), .S(R[1]));
  full_adder full_adder_4 (.A(D1[5]), .B(D2[5]), .CI(full_adder_2_co), .CO(full_adder_4_co), .S(R[5]));
  full_adder full_adder_5 (.A(D1[2]), .B(D2[2]), .CI(full_adder_3_co), .CO(full_adder_5_co), .S(R[2]));
  full_adder full_adder_6 (.A(D1[6]), .B(D2[6]), .CI(full_adder_4_co), .CO(full_adder_6_co), .S(R[6]));
  full_adder full_adder_7 (.A(D1[3]), .B(D2[3]), .CI(full_adder_5_co), .CO(full_adder_7_co), .S(R[3]));
  full_adder full_adder_8 (.A(D1[7]), .B(D2[7]), .CI(full_adder_6_co), .CO(carry_out), .S(R[7]));
endmodule

module full_adder (
  input  A,
  input  B,
  input  CI,
  output CO,
  output S
);

  wire half_adder_1_c, half_adder_1_s, half_adder_2_c;

  half_adder half_adder_1 (.A(A), .B(B), .C(half_adder_1_c), .S(half_adder_1_s));
  half_adder half_adder_2 (.A(half_adder_1_s), .B(CI), .C(half_adder_2_c), .S(S));
  or or_1 (CO, half_adder_1_c, half_adder_2_c);
endmodule

module half_adder (
  input  A,
  input  B,
  output C,
  output S
);

  and and_1 (C, A, B);
  xor xor_1 (S, A, B);
endmodule
